// Logisim project 1ZADANIE.circ as structural Verilog: 1 circuit, main circuit main
module main (
  input  A,
  input  B,
  input  C,
  input  D,
  input  B_2,
  input  D_2,
  output out_7,
  output out_8
);

  wire and_1_out, not_1_out, xnor_1_out, xor_1_out;

  not not_1 (not_1_out, D);
  xor xor_1 (xor_1_out, C, not_1_out);
  and and_1 (and_1_out, B_2, D_2);
  xnor xnor_1 (xnor_1_out, A, B);
  nand nand_1 (out_7, xnor_1_out, xor_1_out);
  xnor xnor_2 (out_8, xor_1_out, and_1_out);

  // Notes on the sheet:
  //   XNOR
  //   XOR
  //   AND
  //   NAND
  //   XNOR
endmodule
