// Logisim project 2_zad_machacova.circ as structural Verilog: 1 circuit, main circuit main
module main (
  input  a,
  input  b,
  input  c,
  input  d,
  output A_D,
  output B_D,
  output C_D,
  output D_D,
  output A_K,
  output B_K,
  output C_K,
  output D_K
);

  wire A_B_C_D_out, A_B_nC_nD_out, A_D_out, A_nB_C_nD_out, A_nB_nC_D_out, A_nB_nD_out, A_nD_out, B_C_out,
       B_D_out, B_nC_nD_out, B_nD_out, nA_B_C_D_out, nA_nD_out, na_out, nB_C_nD_out, nB_C_out, nB_nC_D_out,
       nb_out, nc_out, nd_out, nor_1_out, nor_2_out, nor_3_out, nor_4_out;

  nand na (na_out, a, a);
  nor nor_1 (nor_1_out, a, a);
  nand nc (nc_out, c, c);
  nand nb (nb_out, b, b);
  nor nor_2 (nor_2_out, b, b);
  nor nor_3 (nor_3_out, c, c);
  nand nd (nd_out, d, d);
  nor nor_4 (nor_4_out, d, d);
  nand B_nD (B_nD_out, b, nd_out);
  nand u_B_D (B_D_out, b, d);
  nand A_nD (A_nD_out, a, nd_out);
  nand nB_C (nB_C_out, nb_out, c);
  nand nB_nC_D (nB_nC_D_out, nb_out, nc_out, d);
  nand nB_C_nD (nB_C_nD_out, nb_out, c, nd_out);
  nand B_nC_nD (B_nC_nD_out, b, nc_out, nd_out);
  nand nA_B_C_D (nA_B_C_D_out, na_out, b, c, d);
  nor u_A_D (A_D_out, a, d);
  nor B_C (B_C_out, b, c);
  nor A_nB_nD (A_nB_nD_out, a, nor_2_out, nor_4_out);
  nor nA_nD (nA_nD_out, nor_1_out, nor_4_out);
  nor A_B_C_D (A_B_C_D_out, a, b, c, d);
  nor A_nB_C_nD (A_nB_C_nD_out, a, nor_2_out, c, nor_4_out);
  nor A_B_nC_nD (A_B_nC_nD_out, a, b, nor_3_out, nor_4_out);
  nor A_nB_nC_D (A_nB_nC_D_out, a, nor_2_out, nor_3_out, d);
  nor out_B (B_K, nor_2_out, A_D_out);
  nor out_C (C_K, B_C_out, A_nB_nD_out);
  nand out_A (A_D, B_nD_out, B_D_out);
  nand out_B_2 (B_D, B_D_out, A_nD_out);
  nand out_C_2 (C_D, B_nD_out, na_out, nB_C_out);
  nand out_D (D_D, A_nD_out, nB_nC_D_out, nB_C_nD_out, B_nC_nD_out, nA_B_C_D_out);
  nor out_D_2 (D_K, nA_nD_out, A_B_C_D_out, A_nB_C_nD_out, A_B_nC_nD_out, A_nB_nC_D_out);

  assign A_K = b;

  // Notes on the sheet:
  //   out A
endmodule
