// Logisim project 1_zad.circ as structural Verilog: 1 circuit, main circuit main
module main (
  input  A,
  input  B,
  input  C,
  input  D,
  output Y_zad,
  output Y_DNF,
  output Y_KNF,
  output Z_zad,
  output Z_DNF,
  output Z_KNF
);

  wire A_nB_out, AND_out, C_nD_out, CB_out, nAB_out, nC_nBD_out, nCD_out, not_1_out, not_2_out, not_3_out,
       not_4_out, not_5_out, not_6_out, not_7_out, not_8_out, not_9_out, or_1_out, or_2_out, or_3_out,
       or_4_out, or_5_out, or_6_out, or_7_out, or_8_out, XNOR_out, XOR_out;

  not not_1 (not_1_out, A);
  not not_2 (not_2_out, B);
  not not_3 (not_3_out, C);
  not not_4 (not_4_out, D);
  not not_5 (not_5_out, A);
  not not_6 (not_6_out, B);
  not not_7 (not_7_out, C);
  not not_8 (not_8_out, D);
  not not_9 (not_9_out, D);
  xnor XNOR (XNOR_out, A, B);
  xor XOR (XOR_out, C, not_9_out);
  and AND (AND_out, B, D);
  nand NAND (Y_zad, XNOR_out, XOR_out);
  xnor XNOR_2 (Z_zad, XOR_out, AND_out);
  and nAB (nAB_out, not_1_out, B);
  and A_nB (A_nB_out, A, not_2_out);
  and nCD (nCD_out, not_3_out, D);
  and C_nD (C_nD_out, C, not_4_out);
  and nC_nBD (nC_nBD_out, not_2_out, not_3_out, D);
  and CB (CB_out, B, C);
  or or_1 (or_1_out, A, B, C, D);
  or or_2 (or_2_out, A, B, not_7_out, not_8_out);
  or or_3 (or_3_out, not_5_out, not_6_out, C, D);
  or or_4 (or_4_out, not_5_out, not_6_out, not_7_out, not_8_out);
  or or_5 (or_5_out, B, C, D);
  or or_6 (or_6_out, B, not_7_out, not_8_out);
  or or_7 (or_7_out, not_6_out, C, D);
  or or_8 (or_8_out, not_6_out, C, not_8_out);
  or OR_9 (Y_DNF, nAB_out, A_nB_out, nCD_out, C_nD_out);
  or OR_10 (Z_DNF, C_nD_out, nC_nBD_out, CB_out);
  and AND_2 (Y_KNF, or_1_out, or_2_out, or_3_out, or_4_out);
  and AND_3 (Z_KNF, or_5_out, or_6_out, or_7_out, or_8_out);

  // Notes on the sheet:
  //   A           B           C          D
  //   !A
  //   !B
  //   !C
  //   !D
  //   !A   !B    !C   !D
  //   !A   !B    !C   !D
  //   Y
  //   C!D
  //   A+B+C+D
  //   A+B+ !C + !D
  //   !A + !B +C+D
  //   !A + !B + !C + !D
  //   B+C+D
  //   B+ !C + !D
  //   !B +C+D
  //   !B +C+ !D
  //   Z
  //   Y
  //   Z
endmodule
