// Logisim project 3_zadanie_machacova.circ as structural Verilog: 1 circuit, main circuit main
module main (
  input  X,
  input  RES,
  output Y
);

  wire clock_1_out, j_k_ff_1_q, j_k_ff_1_qn, j_k_ff_2_q, j_k_ff_2_qn, j_k_ff_3_q, nand_1_out, nand_3_out,
       nand_4_out, nand_5_out, nand_6_out, nand_7_out, nand_8_out, nand_9_out, nand_10_out, nand_11_out,
       nand_12_out, nand_13_out, nand_14_out, nand_15_out, nand_16_out, nand_17_out, nand_18_out;

  nand nand_1 (nand_1_out, X, X);
  Clock clock_1 (.out(clock_1_out));
  nand nand_2 (Y, nand_3_out, nand_3_out);
  nand nand_3 (nand_3_out, nand_1_out, j_k_ff_1_q, j_k_ff_2_q);
  nand nand_4 (nand_4_out, nand_1_out, j_k_ff_2_q, j_k_ff_3_q);
  nand nand_5 (nand_5_out, X, j_k_ff_2_qn);
  nand nand_6 (nand_6_out, j_k_ff_1_q, j_k_ff_2_q);
  nand nand_7 (nand_7_out, X, j_k_ff_1_qn, j_k_ff_3_q);
  nand nand_8 (nand_8_out, nand_1_out, j_k_ff_1_q, j_k_ff_3_q);
  nand nand_9 (nand_9_out, nand_1_out, j_k_ff_1_qn, j_k_ff_2_q);
  nand nand_10 (nand_10_out, X, j_k_ff_1_q);
  nand nand_11 (nand_11_out, j_k_ff_1_q, j_k_ff_2_qn);
  nand nand_12 (nand_12_out, j_k_ff_2_qn, j_k_ff_1_qn);
  nand nand_13 (nand_13_out, nand_4_out, nand_4_out);
  nand nand_14 (nand_14_out, nand_5_out, nand_6_out);
  nand nand_15 (nand_15_out, nand_7_out, nand_8_out);
  nand nand_16 (nand_16_out, nand_4_out, nand_6_out, nand_7_out);
  nand nand_17 (nand_17_out, nand_9_out, nand_10_out, nand_5_out, nand_11_out);
  nand nand_18 (nand_18_out, nand_8_out, nand_9_out, nand_12_out);
  J_K_Flip_Flop j_k_ff_1 (
    .J(nand_13_out), .clk(clock_1_out), .K(nand_14_out), .Q(j_k_ff_1_q), .Qn(j_k_ff_1_qn), .reset(RES));  // open: preset, en
  J_K_Flip_Flop j_k_ff_2 (
    .J(nand_15_out), .clk(clock_1_out), .K(nand_16_out), .Q(j_k_ff_2_q), .Qn(j_k_ff_2_qn), .reset(RES));  // open: preset, en
  J_K_Flip_Flop j_k_ff_3 (
    .J(nand_17_out), .clk(clock_1_out), .K(nand_18_out), .Q(j_k_ff_3_q), .reset(RES));  // open: Qn, preset, en
endmodule
